# Fritzing sketch adruino-pour-le-cone (saved by Fritzing 0.9.3b)

parts:
  Boutton_activer_par_le_levier_du_cone = Pushbutton [package="[SMD]"]
  WeMos_D1_Mini_Relay_Shield_V3 = WeMos D1 Mini Relay Shield V2
  Composant4 = Arduino Uno (Rev3) - ICSP
  Composant5 = NRF24L01+ Breakout Board
  C2 = Electrolytic Capacitor [capacitance=1µF package="100 mil [THT, electrolytic]"]
  lumiere_dalerte_blanche = smd LED [color="White (8000K)" package="1206 [SMD]"]
  WeMos_D1_Mini_Relay_Shield_V2 = WeMos D1 Mini Relay Shield V2
  battery_de_la_machine_24volt = Battery block 9V

nets:
  GND: Boutton_activer_par_le_levier_du_cone.Pin_1, Boutton_activer_par_le_levier_du_cone.Pin_2, WeMos_D1_Mini_Relay_Shield_V3.NC, Composant4.GND, Composant5.GND, C2.-, battery_de_la_machine_24volt.-
  N1: Boutton_activer_par_le_levier_du_cone.Pin_3, Boutton_activer_par_le_levier_du_cone.Pin_4, Composant4.D7
  5V: WeMos_D1_Mini_Relay_Shield_V3.5V, Composant4.5V
  N2: WeMos_D1_Mini_Relay_Shield_V3.COM, lumiere_dalerte_blanche.cathode
  N3: WeMos_D1_Mini_Relay_Shield_V3.D4, Composant4.D4
  N4: Composant4.ICSP_MISO, Composant4.D12/MISO, Composant5.MISO
  N5: Composant4.D8, Composant5.CE
  N6: Composant4.D10_PWM/SS, Composant5.CS
  N7: Composant4.D11_PWM/MOSI, Composant5.MOSI
  N8: Composant4.D13/SCK, Composant5.SCK
  N9: Composant4.D3_PWM, WeMos_D1_Mini_Relay_Shield_V2.D3
  N10: Composant4.3V3, C2.+

notes:
  Arduino CONE
  fil de ground du solenoid qui active le levier pour strat ou stop le feeder du cone
  je me sert du relay pour faire comme si je coupais le fil alors le solenoid tombe a off se qui stop le feeder et par le fait meme apuis sur le boutton relier au arduino
