# Fritzing sketch adruino-pour-le-primaire (saved by Fritzing 0.9.3b)

parts:
  Composant4 = Arduino Uno (Rev3) - ICSP
  Composant5 = NRF24L01+ Breakout Board
  C2 = Electrolytic Capacitor [capacitance=1µF package="100 mil [THT, electrolytic]"]
  WeMos_D1_Mini_Relay_Shield_V2 = WeMos D1 Mini Relay Shield V2

nets:
  N1: Composant4.ICSP_MISO, Composant4.D12/MISO, Composant5.MISO
  GND: Composant4.GND, Composant5.GND, C2.-
  N2: Composant4.D8, Composant5.CE
  N3: Composant4.D10_PWM/SS, Composant5.CS
  N4: Composant4.D11_PWM/MOSI, Composant5.MOSI
  N5: Composant4.D13/SCK, Composant5.SCK
  N6: Composant4.D5_PWM, WeMos_D1_Mini_Relay_Shield_V2.D5
  N7: Composant4.3V3, C2.+
  5V: Composant4.5V, WeMos_D1_Mini_Relay_Shield_V2.5V

notes:
  Arduino Primaire
  fil de ground du solenoid qui active le levier pour strart ou stop le feeder du primaire
