# Fritzing sketch adruino-pour-le-tamis (saved by Fritzing 0.9.3b)

parts:
  WeMos_D1_Mini_Relay_Shield_V3 = WeMos D1 Mini Relay Shield V2
  Composant4 = Arduino Uno (Rev3) - ICSP
  Composant5 = NRF24L01+ Breakout Board
  C2 = Electrolytic Capacitor [capacitance=1µF package="100 mil [THT, electrolytic]"]
  WeMos_D1_Mini_Relay_Shield_V2 = WeMos D1 Mini Relay Shield V2
  Sensor_hall_effect_pour_conaitre_le_rpm_dune_roue_denteler_sur_la_machine = HALL-EFFECT [package=sc70]
  battery_de_la_machine_24volt = Battery block 9V
  WeMos_D1_Mini_Relay_Shield_V4 = WeMos D1 Mini Relay Shield V2
  WeMos_D1_Mini_Relay_Shield_V5 = WeMos D1 Mini Relay Shield V2  # not connected

nets:
  5V: WeMos_D1_Mini_Relay_Shield_V3.5V, Composant4.5V
  N1: WeMos_D1_Mini_Relay_Shield_V3.D4, Composant4.D4
  N2: Composant4.ICSP_MISO, Composant4.D12/MISO, Composant5.MISO
  GND: Composant4.GND, Composant5.GND, C2.-, Sensor_hall_effect_pour_conaitre_le_rpm_dune_roue_denteler_sur_la_machine.OUT, battery_de_la_machine_24volt.-, battery_de_la_machine_24volt.+, WeMos_D1_Mini_Relay_Shield_V4.COM
  N3: Composant4.D8, Composant5.CE
  N4: Composant4.D9_PWM, Sensor_hall_effect_pour_conaitre_le_rpm_dune_roue_denteler_sur_la_machine.GND
  N5: Composant4.D10_PWM/SS, Composant5.CS
  N6: Composant4.D11_PWM/MOSI, Composant5.MOSI
  N7: Composant4.D13/SCK, Composant5.SCK
  N8: Composant4.D6_PWM, WeMos_D1_Mini_Relay_Shield_V2.D6
  N9: Composant4.3V3, C2.+

notes:
  Arduino Tamis
  Cylindre electrique pour activer et desactiver le levier qui stop tout sur la machine et il doit faire un aller retour pour stop toutpour ca le cablage a 4 relay
  conecter au positif de la battery meme si fritzing veux pas :)
