# Fritzing sketch emetteur_nrf24l01_V2 (saved by Fritzing 0.9.3b)

parts:
  Composant1 = Arduino Uno (Rev3) - ICSP
  Composant3 = NRF24L01+ Breakout Board
  STOP_ALL = SWITCH-MOMENTARY-2 [package=tactile_switch_tall]
  STOP_CONE = SWITCH-MOMENTARY-2 [package=tactile_switch_tall]
  START_CONE = SWITCH-MOMENTARY-2 [package=tactile_switch_tall]
  STOP_PRIMARY = SWITCH-MOMENTARY-2 [package=tactile_switch_tall]
  START_PRIMARY = SWITCH-MOMENTARY-2 [package=tactile_switch_tall]
  R4 = Resistor [tolerance=±5% resistance=220 package=THT]
  C1 = Electrolytic Capacitor [capacitance=1µF package="100 mil [THT, electrolytic]"]
  R7 = Resistor [tolerance=±5% resistance=220 package=THT]
  R8 = Resistor [tolerance=±5% resistance=220 package=THT]
  CONE_COMMUNICATION_OK = smd LED [color="Red (633nm)" package="1206 [SMD]"]
  TAMIS_COMMUNICATION_OK = smd LED [color="Red (633nm)" package="1206 [SMD]"]
  PRIMARY_COMMUNICATION_OK = smd LED [color="Red (633nm)" package="1206 [SMD]"]

nets:
  N1: Composant1.A0, R8.Pin_0
  N2: Composant1.A1, R7.Pin_0
  N3: Composant1.A2, R4.Pin_0
  N4: Composant1.ICSP_MISO, Composant1.D12/MISO, Composant3.MISO
  N5: Composant1.D8, Composant3.CE
  N6: Composant1.D10_PWM/SS, Composant3.CS
  N7: Composant1.D11_PWM/MOSI, Composant3.MOSI
  N8: Composant1.D13/SCK, Composant3.SCK
  GND: Composant1.GND, Composant3.GND, C1.-
  N9: Composant1.D2, STOP_ALL.2
  N10: Composant1.D3_PWM, STOP_CONE.2
  N11: Composant1.D4, START_CONE.2
  N12: Composant1.D6_PWM, STOP_PRIMARY.2
  N13: Composant1.D7, START_PRIMARY.2
  N14: Composant3.VCC, C1.+
  N15: STOP_ALL.1, CONE_COMMUNICATION_OK.cathode, TAMIS_COMMUNICATION_OK.cathode, PRIMARY_COMMUNICATION_OK.cathode

notes:
  Arduino Principal
